# Fritzing sketch proj (saved by Fritzing 0.9.10b)
circuit board: 8.46667cm x 5.64444cm
breadboards: 1

parts:
  A1 = Teensy 4.1
  Part1 = Adafruit TB6612 DC and Stepper Motor Driver [part_number="Adafruit #2448"]
  Part2 = Adafruit TB6612 DC and Stepper Motor Driver [part_number="Adafruit #2448"]
  U1 = SLIDER [knob_status=50% power=0.5W package=slider]
  U2 = SLIDER [knob_status=50% power=0.5W package=slider]
  U4 = SLIDER [knob_status=50% power=0.5W package=slider]
  M1 = DC Motor [voltage_(max)=6V voltage_(min)=3V]
  M2 = DC Motor [voltage_(max)=6V voltage_(min)=3V]
  M3 = DC Motor [voltage_(max)=6V voltage_(min)=3V]
  M4 = DC Motor [voltage_(max)=6V voltage_(min)=3V]
  VCC1 = Battery block 9V
  U3 = SLIDER [knob_status=50% power=0.5W package=slider]

nets:
  GND: A1.Pin_12, A1.Pin_38, A1.Pin_50, A1.Pin_63, Part1.GND, Part2.GND, VCC1.-
  N1: A1.Pin_13, Part2.AIN1
  N2: A1.Pin_14, Part2.AIN2
  N3: A1.Pin_15, Part2.BIN1
  N4: A1.Pin_16, Part2.BIN2
  N5: A1.Pin_17, Part1.AIN1
  N6: A1.Pin_18, Part1.AIN2
  N7: A1.Pin_19, Part1.BIN1
  N8: A1.Pin_20, Part1.BIN2
  N9: A1.Pin_26, A1.Pin_62, U1.E, U2.E, U4.E, U3.E
  N10: A1.Pin_27, Part1.PWMA
  N11: A1.Pin_28, Part1.PWMB
  N12: A1.Pin_52, U4.S
  N13: A1.Pin_53, U3.S
  N14: A1.Pin_54, U1.S
  N15: A1.Pin_55, U2.S
  N16: A1.Pin_60, Part2.PWMA
  N17: A1.Pin_61, Part2.PWMB
  N18: Part1.Vmotor, Part1.PWRIN, Part2.Vmotor, Part2.PWRIN, VCC1.+
  VCC: Part1.VCC, Part1.STBY, Part2.VCC, Part2.STBY
  N19: Part1.MOTORA1, M2.pin_2
  N20: Part1.MOTORA2, M2.pin_1
  N21: Part1.MOTORB2, M1.pin_1
  N22: Part1.MOTORB1, M1.pin_2
  N23: Part2.MOTORA1, M3.pin_2
  N24: Part2.MOTORA2, M3.pin_1
  N25: Part2.MOTORB2, M4.pin_1
  N26: Part2.MOTORB1, M4.pin_2
  N27: U1.A, U2.A, U4.A, U3.A

custom parts:
  Teensy 4.1: The Teensy is a complete USB-based microcontoller development system, in a very small footprint, capable of implementing many types of projects. All programming is done via the USB port. No special programmer is needed, only a standard micro-USB cable and a PC or Macintosh with a USB port.
  Adafruit TB6612 DC and Stepper Motor Driver: Spin two DC motors, step one bi-polar or uni-polar stepper, or fire off two solenoids with 1.2A per channel using the TB6612. These are perhaps better known as "the drivers in our assembled Adafruit Motorshield or Motor HAT." We really like these dual H-bridges, so if you want to control motors without a shield or HAT these are easy to include on any solderless breadboard or perma-proto.
